# Fritzing sketch pcb (saved by Fritzing 0.9.3b)
breadboards: 1

parts:
  U1 = atmega328 [package=dip]
  C1 = Ceramic Capacitor [capacitance=20µF package="0805 [SMD, multilayer]"]
  C2 = Ceramic Capacitor [capacitance=20µF package="0805 [SMD, multilayer]"]
  Part1 = XBee USB Mini Adapter
  C3 = Ceramic Capacitor [capacitance="100 nF" package="0603 [SMD, multilayer]"]
  XTAL1 = Crystal [frequency="16 Mhz" package=THT]
  J1 = Basic Servo
  Part2 = Bluetooth HC-05 Macho

nets:
  N1: U1.RESET, C3.0
  N2: U1.D0_(RX), Part1.TXD, Part2.RXD
  N3: U1.D1_(TX), Part1.RXD, Part2.TXD
  VCC: U1.VCC, Part1.5V
  N4: U1.GND#7, C1.0, C2.0
  N5: U1.XLAT1, C1.1, XTAL1.pin_0
  N6: U1.XLAT2, C2.1, XTAL1.pin_1
  N7: U1.D13, J1.pulse
  VCC_2: U1.AVCC, J1.vcc, Part2.VCC
  GND: U1.GND#21, Part1.GND, J1.gnd, Part2.GND
  N8: Part1.RST, C3.1
